# Fritzing sketch mail_detection (saved by Fritzing 0.9.3b)

parts:
  LED1 = LEDs [package=led10mm]
  R1 = PHOTOCELL [package=photocell-kit]
  R2 = PHOTOCELL [package=photocell-kit]
  R3 = PHOTOCELL [package=photocell-kit]
  R4 = PHOTOCELL [package=photocell-kit]
  R5 = PHOTOCELL [package=photocell-kit]
  R6 = PHOTOCELL [package=photocell-kit]
  Part2 = Bluetooth HC-05 Macho
  R7 = Resistor [tolerance=±5% resistance=220 package="2010 [SMD]"]
  R8 = Resistor [tolerance=±5% resistance=220 package="2010 [SMD]"]
  R9 = Resistor [tolerance=±5% resistance=220 package="2010 [SMD]"]
  R10 = Resistor [tolerance=±5% resistance=220 package="2010 [SMD]"]
  R11 = Resistor [tolerance=±5% resistance=220 package="2010 [SMD]"]
  R12 = Resistor [tolerance=±5% resistance=220 package="2010 [SMD]"]
  Part1 = Arduino Uno (Rev3) - ICSP

nets:
  GND: LED1.C, R1.P$2, R2.P$2, R3.P$2, R4.P$2, R5.P$2, R6.P$2, Part2.GND, Part1.GND
  N1: LED1.A, Part1.D13/SCK
  N2: R1.P$1, R12.Pin_1, Part1.A5/SCL
  N3: R2.P$1, R10.Pin_1, Part1.A3
  N4: R3.P$1, R9.Pin_1, Part1.A2
  N5: R4.P$1, R11.Pin_1, Part1.A4/SDA
  N6: R5.P$1, R8.Pin_1, Part1.A1
  N7: R6.P$1, R7.Pin_1, Part1.A0
  N8: Part2.TXD, Part1.D6_PWM
  N9: Part2.RXD, Part1.D5_PWM
  VCC: Part2.VCC, Part1.3V3
  N10: R7.Pin_0, R8.Pin_0, R9.Pin_0, R10.Pin_0, R11.Pin_0, R12.Pin_0, Part1.5V
